// Logisim project 8bitCPU.circ as structural Verilog: 20 circuits, main circuit 1bitALU
module PEC_1 (
  input  in_1,
  input  in_2,
  input  in_3,
  input  in_4,
  input  in_5,
  input  in_6,
  input  in_7,
  input  in_8,
  output out_9,
  output out_10,
  output out_11,
  output out_12,
  output out_13,
  output out_14
);

  wire A, A1, A2, A3, A4, A5, A6, alu_1_overflow_flag, alu_1_sign_flag, alu_1_zeroflag, B, B1, B2, B3, B4,
       B5, B6, C, C1, C2, C3, C4, C5, C6, D, D1, D2, D3, D4, D5, D6, decoder_1_out_24, decoder_1_out_25, E,
       im1, im2, im3, im4, im5, im6, ld0, ld1, ld2, ld3, ldo, ldpc, n8_6_multiplexer_1_y1,
       n8_6_multiplexer_1_y2, n8_6_multiplexer_1_y3, n8_6_multiplexer_1_y4, n8_6_multiplexer_1_y5,
       n8_6_multiplexer_1_y6, n8_6_multiplexer_2_y1, n8_6_multiplexer_2_y2, n8_6_multiplexer_2_y3,
       n8_6_multiplexer_2_y4, n8_6_multiplexer_2_y5, n8_6_multiplexer_2_y6, op0, op1, op2, op3, ora0, ora1,
       orb0, orb1, register_6_q, register_7_q, register_8_q, sela0, sela1, sela2, selb0, selb1, selb2, Y1,
       Y2, Y3, Y4, Y5, Y6;

  Clock clock_1 ();  // open: out
  Register register_1 (
    .CLK(in_1), .A(Y1), .B(Y2), .C(Y3), .D(Y4), .E(Y5), .F(Y6), .ENB(ld0), .CLR(in_8), .Y1(A1), .Y2(A2),
    .Y3(A3), .Y4(A4), .Y5(A5), .Y6(A6));
  Register register_2 (
    .CLK(in_1), .A(Y1), .B(Y2), .C(Y3), .D(Y4), .E(Y5), .F(Y6), .ENB(ld1), .CLR(in_8), .Y1(B1), .Y2(B2),
    .Y3(B3), .Y4(B4), .Y5(B5), .Y6(B6));
  Register register_3 (
    .CLK(in_1), .A(Y1), .B(Y2), .C(Y3), .D(Y4), .E(Y5), .F(Y6), .ENB(ld2), .CLR(in_8), .Y1(C1), .Y2(C2),
    .Y3(C3), .Y4(C4), .Y5(C5), .Y6(C6));
  Register register_4 (
    .CLK(in_1), .A(Y1), .B(Y2), .C(Y3), .D(Y4), .E(Y5), .F(Y6), .ENB(ld3), .CLR(in_8), .Y1(D1), .Y2(D2),
    .Y3(D3), .Y4(D4), .Y5(D5), .Y6(D6));
  Register register_5 (
    .CLK(in_1), .A(Y1), .B(Y2), .C(Y3), .D(Y4), .E(Y5), .F(Y6), .ENB(ldo), .CLR(in_8), .Y1(out_14),
    .Y2(out_13), .Y3(out_12), .Y4(out_11), .Y5(out_10), .Y6(out_9));
  regpc regpc_1 (
    .CLR(in_8), .LOAD(ldpc), .CNT(1'b1), .A(Y1), .B(Y2), .C(Y3), .D(Y4), .E(Y5), .QA(A), .QB(B), .QC(C),
    .QD(D), .QE(E), .CLK(in_1));  // open: in_10, QF
  ROM #(.addrWidth(5), .dataWidth(14)) rom_1 (
    .addr({E, D, C, B, A}), .data({op3, op2, op1, op0, ora1, ora0, orb1, orb0, im6, im5, im4, im3, im2, im1}));  // open: sel
  _8_6_multiplexer u_8_6_multiplexer_1 (
    .A1(A1), .B1(B1), .C1(C1), .D1(D1), .E1(in_2), .F1(im1), .A2(A2), .B2(B2), .C2(C2), .D2(D2), .E2(in_3),
    .F2(im2), .A3(A3), .B3(B3), .C3(C3), .D3(D3), .E3(in_4), .F3(im3), .A4(A4), .B4(B4), .C4(C4), .D4(D4),
    .E4(in_5), .F4(im4), .A5(A5), .B5(B5), .C5(C5), .D5(D5), .E5(in_6), .F5(im5), .A6(A6), .B6(B6), .C6(C6),
    .D6(D6), .E6(in_7), .F6(im6), .Y1(n8_6_multiplexer_1_y1), .Y2(n8_6_multiplexer_1_y2),
    .Y3(n8_6_multiplexer_1_y3), .Y4(n8_6_multiplexer_1_y4), .Y5(n8_6_multiplexer_1_y5),
    .Y6(n8_6_multiplexer_1_y6), .S3(sela2), .S2(sela1), .S1(sela0), .G1(1'b0), .G3(1'b0), .G4(1'b0),
    .G5(1'b0), .G2(1'b0), .G6(1'b0));  // open: H1, H2, H3, H4, H5, H6
  _8_6_multiplexer u_8_6_multiplexer_2 (
    .A1(A1), .B1(B1), .C1(C1), .D1(D1), .E1(in_2), .F1(im1), .A2(A2), .B2(B2), .C2(C2), .D2(D2), .E2(in_3),
    .F2(im2), .A3(A3), .B3(B3), .C3(C3), .D3(D3), .E3(in_4), .F3(im3), .A4(A4), .B4(B4), .C4(C4), .D4(D4),
    .E4(in_5), .F4(im4), .A5(A5), .B5(B5), .C5(C5), .D5(D5), .E5(in_6), .F5(im5), .A6(A6), .B6(B6), .C6(C6),
    .D6(D6), .E6(in_7), .F6(im6), .Y1(n8_6_multiplexer_2_y1), .Y2(n8_6_multiplexer_2_y2),
    .Y3(n8_6_multiplexer_2_y3), .Y4(n8_6_multiplexer_2_y4), .Y5(n8_6_multiplexer_2_y5),
    .Y6(n8_6_multiplexer_2_y6), .S3(selb2), .S2(selb1), .S1(selb0), .G1(1'b0), .G3(1'b0), .G4(1'b0),
    .G5(1'b0), .G2(1'b0), .G6(1'b0));  // open: H1, H2, H3, H4, H5, H6
  ALU alu_1 (
    .A1(n8_6_multiplexer_1_y1), .B1(n8_6_multiplexer_2_y1), .A2(n8_6_multiplexer_1_y2),
    .B2(n8_6_multiplexer_2_y2), .A3(n8_6_multiplexer_1_y3), .B3(n8_6_multiplexer_2_y3),
    .A4(n8_6_multiplexer_1_y4), .B4(n8_6_multiplexer_2_y4), .A5(n8_6_multiplexer_1_y5),
    .B5(n8_6_multiplexer_2_y5), .A6(n8_6_multiplexer_1_y6), .B6(n8_6_multiplexer_2_y6), .Y1(Y1), .Y2(Y2),
    .Y3(Y3), .Y4(Y4), .Y5(Y5), .Y6(Y6), .A_L(decoder_1_out_25), .in_2(decoder_1_out_24),
    .Sign_Flag(alu_1_sign_flag), .OverFlow_Flag(alu_1_overflow_flag), .ZeroFlag(alu_1_zeroflag));  // open: Carry_Flag
  Register_part #(.width(1)) register_6 (.D(alu_1_zeroflag), .en(1'b1), .Q(register_6_q), .clk(in_1));  // open: clr
  Register_part #(.width(1)) register_7 (
    .D(alu_1_overflow_flag), .en(1'b1), .Q(register_7_q), .clk(in_1));  // open: clr
  Register_part #(.width(1)) register_8 (.D(alu_1_sign_flag), .en(1'b1), .Q(register_8_q), .clk(in_1));  // open: clr
  decoder decoder_1 (
    .op3(op3), .op2(op2), .op1(op1), .op0(op0), .ora1(ora1), .ora0(ora0), .orb1(orb1), .orb0(orb0),
    .ZF(register_6_q), .OF(register_7_q), .SF(register_8_q), .sela2(sela2), .sela1(sela1), .sela0(sela0),
    .ld0(ld0), .selb2(selb2), .ld1(ld1), .selb1(selb1), .ld2(ld2), .selb0(selb0), .ld3(ld3), .ldo(ldo),
    .ldpc(ldpc), .out_25(decoder_1_out_25), .out_24(decoder_1_out_24));

  // Other names for the same wires on the sheet: CLOCK = in_1; CLR_tilde = in_8; E1 = in_2; E2 = in_3; E3 = in_4;
  //   E4 = in_5; E5 = in_6; E6 = in_7

  // Notes on the sheet:
  //   contents of rom_1 (hex, n*v repeats v):
  //   c01 d02 1840 a00 3e00
endmodule

// ALU
module _1bitALU (
  input  A_L,
  input  in_2,
  input  Ci,
  input  A,
  input  B,
  output R,
  output Co
);

  wire and_1_out, and_2_out, and_3_out, and_4_out, and_5_out, and_6_out, fulladder_1_s, nand_1_out,
       not_1_out, not_2_out, not_3_out, xor_1_out;

  not not_1 (not_1_out, A_L);
  and and_1 (and_1_out, not_1_out, in_2);
  not not_2 (not_2_out, A_L);
  and and_2 (and_2_out, not_2_out, A);
  and and_3 (and_3_out, A_L, A);
  not not_3 (not_3_out, A_L);
  and and_4 (and_4_out, not_3_out, B);
  and and_5 (and_5_out, A_L, B);
  xor xor_1 (xor_1_out, and_4_out, and_1_out);
  FullAdder fulladder_1 (.X(and_2_out), .Y(xor_1_out), .S(fulladder_1_s), .Cin(Ci), .Cout(Co));
  nand nand_1 (nand_1_out, and_3_out, and_5_out);
  and and_6 (and_6_out, nand_1_out, A_L);
  or or_1 (R, fulladder_1_s, and_6_out);
endmodule

module ALU (
  input  A_L,
  input  in_2,
  input  A1,
  input  B1,
  input  A2,
  input  B2,
  input  A3,
  input  B3,
  input  A4,
  input  B4,
  input  A5,
  input  B5,
  input  A6,
  input  B6,
  output Y1,
  output Y2,
  output Y3,
  output Y4,
  output Y5,
  output Y6,
  output Carry_Flag,
  output OverFlow_Flag,
  output ZeroFlag,
  output Sign_Flag
);

  wire and_2_out, and_3_out, n1bitalu_1_co, n1bitalu_2_co, n1bitalu_3_co, n1bitalu_4_co, n1bitalu_5_co,
       nor_1_out, nor_2_out, nor_3_out, not_1_out;

  _1bitALU u_1bitalu_1 (.A(A1), .B(B1), .R(Y1), .A_L(A_L), .in_2(in_2), .Ci(in_2), .Co(n1bitalu_1_co));
  _1bitALU u_1bitalu_2 (.A(A2), .B(B2), .R(Y2), .A_L(A_L), .in_2(in_2), .Ci(n1bitalu_1_co), .Co(n1bitalu_2_co));
  _1bitALU u_1bitalu_3 (.A(A3), .B(B3), .R(Y3), .A_L(A_L), .in_2(in_2), .Ci(n1bitalu_2_co), .Co(n1bitalu_3_co));
  _1bitALU u_1bitalu_4 (.A(A4), .B(B4), .R(Y4), .A_L(A_L), .in_2(in_2), .Ci(n1bitalu_3_co), .Co(n1bitalu_4_co));
  _1bitALU u_1bitalu_5 (.A(A5), .B(B5), .R(Y5), .A_L(A_L), .in_2(in_2), .Ci(n1bitalu_4_co), .Co(n1bitalu_5_co));
  _1bitALU u_1bitalu_6 (.A(A6), .B(B6), .R(Y6), .A_L(A_L), .in_2(in_2), .Ci(n1bitalu_5_co), .Co(Carry_Flag));
  xor xor_1 (OverFlow_Flag, n1bitalu_5_co, Carry_Flag);
  and and_1 (Sign_Flag, Y6, not_1_out);
  nor nor_1 (nor_1_out, Y1, Y2);
  nor nor_2 (nor_2_out, Y3, Y4);
  nor nor_3 (nor_3_out, Y5, Y6);
  not not_1 (not_1_out, OverFlow_Flag);
  and and_2 (and_2_out, nor_1_out, nor_2_out);
  and and_3 (and_3_out, and_2_out, nor_3_out);
  and and_4 (ZeroFlag, and_3_out, not_1_out);
endmodule

// 46mp
module _4_6bit_multiplexer (
  input  S2,
  input  S1,
  input  A1,
  input  B1,
  input  C1,
  input  D1,
  input  A2,
  input  B2,
  input  C2,
  input  D2,
  input  A3,
  input  B3,
  input  C3,
  input  D3,
  input  A4,
  input  B4,
  input  C4,
  input  D4,
  input  A5,
  input  B5,
  input  C5,
  input  D5,
  input  A6,
  input  B6,
  input  C6,
  input  D6,
  output Y1,
  output Y2,
  output Y3,
  output Y4,
  output Y5,
  output Y6
);

  _4_1_2mulchiplexer u_4_1_2mulchiplexer_1 (
    .A1(A1), .B1(B1), .C1(C1), .D1(D1), .A2(A2), .B2(B2), .C2(C2), .D2(D2), .Y1(Y1), .Y2(Y2), .S2(S2), .S1(S1));
  _4_1_2mulchiplexer u_4_1_2mulchiplexer_2 (
    .A1(A3), .B1(B3), .C1(C3), .D1(D3), .A2(A4), .B2(B4), .C2(C4), .D2(D4), .Y1(Y3), .Y2(Y4), .S2(S2), .S1(S1));
  _4_1_2mulchiplexer u_4_1_2mulchiplexer_3 (
    .A1(A5), .B1(B5), .C1(C5), .D1(D5), .A2(A6), .B2(B6), .C2(C6), .D2(D6), .Y1(Y5), .Y2(Y6), .S2(S2), .S1(S1));
endmodule

module _8_6_multiplexer (
  input  S3,
  input  S2,
  input  S1,
  input  A1,
  input  B1,
  input  C1,
  input  D1,
  input  E1,
  input  F1,
  input  G1,
  input  H1,
  input  A2,
  input  B2,
  input  C2,
  input  D2,
  input  E2,
  input  F2,
  input  G2,
  input  H2,
  input  A3,
  input  B3,
  input  C3,
  input  D3,
  input  E3,
  input  F3,
  input  G3,
  input  H3,
  input  A4,
  input  B4,
  input  C4,
  input  D4,
  input  E4,
  input  F4,
  input  G4,
  input  H4,
  input  A5,
  input  B5,
  input  C5,
  input  D5,
  input  E5,
  input  F5,
  input  G5,
  input  H5,
  input  A6,
  input  B6,
  input  C6,
  input  D6,
  input  E6,
  input  F6,
  input  G6,
  input  H6,
  output Y1,
  output Y2,
  output Y3,
  output Y4,
  output Y5,
  output Y6
);

  _8_1multiplexer u_8_1multiplexer_1 (
    .A(A1), .B(B1), .C(C1), .D(D1), .E(E1), .F(F1), .S3(S3), .S2(S2), .S1(S1), .Y(Y1), .G(G1), .H(H1));
  _8_1multiplexer u_8_1multiplexer_2 (
    .A(A2), .B(B2), .C(C2), .D(D2), .E(E2), .F(F2), .S3(S3), .S2(S2), .S1(S1), .Y(Y2), .G(G2), .H(H2));
  _8_1multiplexer u_8_1multiplexer_3 (
    .A(A3), .B(B3), .C(C3), .D(D3), .E(E3), .F(F3), .S3(S3), .S2(S2), .S1(S1), .Y(Y3), .G(G3), .H(H3));
  _8_1multiplexer u_8_1multiplexer_4 (
    .A(A4), .B(B4), .C(C4), .D(D4), .E(E4), .F(F4), .S3(S3), .S2(S2), .S1(S1), .Y(Y4), .G(G4), .H(H4));
  _8_1multiplexer u_8_1multiplexer_5 (
    .A(A5), .B(B5), .C(C5), .D(D5), .E(E5), .F(F5), .S3(S3), .S2(S2), .S1(S1), .Y(Y5), .G(G5), .H(H5));
  _8_1multiplexer u_8_1multiplexer_6 (
    .A(A6), .B(B6), .C(C6), .D(D6), .E(E6), .F(F6), .S3(S3), .S2(S2), .S1(S1), .Y(Y6), .G(G6), .H(H6));
endmodule

// FA
module FullAdder (
  input  Cin,
  input  X,
  input  Y,
  output S,
  output Cout
);

  wire halfadder_1_c0, halfadder_1_s, halfadder_2_c0;

  HalfAdder halfadder_1 (.X(X), .Y(Y), .S(halfadder_1_s), .C0(halfadder_1_c0));
  HalfAdder halfadder_2 (.X(Cin), .Y(halfadder_1_s), .S(S), .C0(halfadder_2_c0));
  or or_1 (Cout, halfadder_2_c0, halfadder_1_c0);
endmodule

// HA
module HalfAdder (
  input  X,
  input  Y,
  output S,
  output C0
);

  xor xor_1 (S, X, Y);
  and and_1 (C0, X, Y);
endmodule

// 412mp
module _4_1_2mulchiplexer (
  input  S2,
  input  S1,
  input  A1,
  input  B1,
  input  C1,
  input  D1,
  input  A2,
  input  B2,
  input  C2,
  input  D2,
  output Y1,
  output Y2
);

  wire and_1_out, and_2_out, and_3_out, and_4_out, and_5_out, and_6_out, and_7_out, and_8_out, not_1_out,
       not_2_out, not_3_out, not_4_out, not_5_out, not_6_out, not_7_out, not_8_out;

  not not_1 (not_1_out, S2);
  not not_2 (not_2_out, S1);
  not not_3 (not_3_out, S2);
  not not_4 (not_4_out, S1);
  not not_5 (not_5_out, S2);
  not not_6 (not_6_out, S1);
  not not_7 (not_7_out, S2);
  not not_8 (not_8_out, S1);
  and and_1 (and_1_out, A1, not_1_out, not_2_out);
  and and_2 (and_2_out, B1, not_3_out, S1);
  and and_3 (and_3_out, C1, S2, not_4_out);
  and and_4 (and_4_out, D1, S1, S2);
  and and_5 (and_5_out, A2, not_5_out, not_6_out);
  and and_6 (and_6_out, B2, not_7_out, S1);
  and and_7 (and_7_out, C2, S2, not_8_out);
  and and_8 (and_8_out, D2, S1, S2);
  or or_1 (Y1, and_1_out, and_2_out, and_3_out, and_4_out);
  or or_2 (Y2, and_5_out, and_6_out, and_7_out, and_8_out);
endmodule

module _8_1multiplexer (
  input  S3,
  input  S2,
  input  S1,
  input  A,
  input  B,
  input  C,
  input  D,
  input  E,
  input  F,
  input  G,
  input  H,
  output Y
);

  wire and_1_out, and_2_out, and_3_out, and_4_out, and_5_out, and_6_out, and_7_out, and_8_out, not_1_out,
       not_2_out, not_3_out, not_4_out, not_5_out, not_6_out, not_7_out, not_8_out, not_9_out, not_10_out,
       not_11_out, not_12_out, or_1_out, or_2_out, or_3_out, or_4_out, or_5_out, or_6_out;

  not not_1 (not_1_out, S3);
  not not_2 (not_2_out, S2);
  not not_3 (not_3_out, S1);
  not not_4 (not_4_out, S3);
  not not_5 (not_5_out, S2);
  not not_6 (not_6_out, S3);
  not not_7 (not_7_out, S1);
  not not_8 (not_8_out, S3);
  not not_9 (not_9_out, S2);
  not not_10 (not_10_out, S1);
  not not_11 (not_11_out, S2);
  not not_12 (not_12_out, S1);
  and and_1 (and_1_out, A, not_1_out, not_2_out, not_3_out);
  and and_2 (and_2_out, B, not_4_out, not_5_out, S1);
  and and_3 (and_3_out, C, not_6_out, S2, not_7_out);
  and and_4 (and_4_out, D, not_8_out, S2, S1);
  and and_5 (and_5_out, E, S3, not_9_out, not_10_out);
  and and_6 (and_6_out, F, S3, not_11_out, S1);
  and and_7 (and_7_out, G, S3, S2, not_12_out);
  and and_8 (and_8_out, H, S3, S2, S1);
  or or_1 (or_1_out, and_1_out, and_2_out);
  or or_2 (or_2_out, and_3_out, and_4_out);
  or or_3 (or_3_out, and_5_out, and_6_out);
  or or_4 (or_4_out, and_7_out, and_8_out);
  or or_5 (or_5_out, or_1_out, or_2_out);
  or or_6 (or_6_out, or_3_out, or_4_out);
  or or_7 (Y, or_5_out, or_6_out);
endmodule

// Reg
module Register (
  input  CLK,
  input  A,
  input  B,
  input  C,
  input  D,
  input  E,
  input  F,
  input  ENB,
  input  CLR,
  output Y1,
  output Y2,
  output Y3,
  output Y4,
  output Y5,
  output Y6
);

  wire not_1_out, not_2_out;

  not not_1 (not_1_out, ENB);
  not not_2 (not_2_out, CLR);
  D_Flip_Flop d_ff_1 (.clk(CLK), .D(A), .Q(Y1), .en(not_1_out), .reset(not_2_out));  // open: Qn, preset
  D_Flip_Flop d_ff_2 (.clk(CLK), .D(B), .Q(Y2), .en(not_1_out), .reset(not_2_out));  // open: Qn, preset
  D_Flip_Flop d_ff_3 (.clk(CLK), .D(C), .Q(Y3), .en(not_1_out), .reset(not_2_out));  // open: Qn, preset
  D_Flip_Flop d_ff_4 (.clk(CLK), .D(D), .Q(Y4), .en(not_1_out), .reset(not_2_out));  // open: Qn, preset
  D_Flip_Flop d_ff_5 (.clk(CLK), .D(E), .Q(Y5), .en(not_1_out), .reset(not_2_out));  // open: Qn, preset
  D_Flip_Flop d_ff_6 (.clk(CLK), .D(F), .Q(Y6), .en(not_1_out), .reset(not_2_out));  // open: Qn, preset
endmodule

module regpc (
  input  CLR,
  input  LOAD,
  input  CLK,
  input  CNT,
  input  A,
  input  B,
  input  C,
  input  D,
  input  E,
  input  in_10,
  output QA,
  output QB,
  output QC,
  output QD,
  output QE,
  output QF
);

  wire and_1_out, n74161_1_co, not_1_out;

  and and_1 (and_1_out, CLR, not_1_out);
  not not_1 (not_1_out, QF);
  _74161 u_74161_1 (
    .CLK(CLK), .LOAD(LOAD), .COUNT(CNT), .CLR(and_1_out), .A(A), .B(B), .C(C), .D(D), .QA(QA), .QB(QB),
    .QC(QC), .QD(QD), .CO(n74161_1_co));
  _74161 u_74161_2 (
    .CLK(CLK), .LOAD(LOAD), .COUNT(n74161_1_co), .CLR(and_1_out), .A(E), .B(in_10), .QA(QE), .QB(QF));  // open: C, D, QC, QD, CO
endmodule

module decoder (
  input  op3,
  input  op2,
  input  op1,
  input  op0,
  input  ora1,
  input  ora0,
  input  orb1,
  input  orb0,
  input  ZF,
  input  OF,
  input  SF,
  output sela2,
  output sela1,
  output sela0,
  output selb2,
  output selb1,
  output selb0,
  output ld0,
  output ld1,
  output ld2,
  output ld3,
  output ldo,
  output ldpc,
  output out_24,
  output out_25
);

  ld0 ld0_1 (
    .op3(op3), .op2(op2), .op1(op1), .op0(op0), .ora1(ora1), .ora0(ora0), .ld0(ld0), .ld1(ld1), .ld2(ld2),
    .ld3(ld3));
  ldo ldo_1 (.op3(op3), .op2(op2), .op1(op1), .op0(op0), .ldo(ldo));
  ldpc ldpc_1 (.op3(op3), .op2(op2), .op1(op1), .op0(op0), .ZF(ZF), .OF(OF), .SF(SF), .ldpc(ldpc));
  alpm alpm_1 (.op3(op3), .op2(op2), .op1(op1), .out_4(out_24), .A_L(out_25));
  sela sela_1 (
    .op3(op3), .op2(op2), .op1(op1), .op0(op0), .ora1(ora1), .ora0(ora0), .orb1(orb1), .orb0(orb0),
    .sela2(sela2), .sela1(sela1), .sela0(sela0));
  selb selb_1 (
    .op3(op3), .op2(op2), .op1(op1), .op0(op0), .orb1(orb1), .orb0(orb0), .selb2(selb2), .selb1(selb1),
    .selb0(selb0));
endmodule

module _74161 (
  input  CLK,
  input  LOAD,
  input  COUNT,
  input  CLR,
  input  A,
  input  B,
  input  C,
  input  D,
  output QA,
  output QB,
  output QC,
  output QD,
  output CO
);

  wire and_1_out, and_2_out, and_4_out, not_1_out, not_2_out;

  not not_1 (not_1_out, LOAD);
  not not_2 (not_2_out, CLR);
  and and_1 (and_1_out, not_1_out, CLR);
  and and_2 (and_2_out, LOAD, CLR, COUNT);
  and and_3 (CO, and_4_out, and_2_out);
  Counter #(.width(4), .max('hf)) counter_1 (
    .load(and_1_out), .D({D, C, B, A}), .count(and_2_out), .Q({QD, QC, QB, QA}), .clk(CLK), .clr(not_2_out));  // open: carry
  and and_4 (and_4_out, QA, QB, QC, QD);
endmodule

module ld0 (
  input  op3,
  input  op2,
  input  op1,
  input  op0,
  input  ora1,
  input  ora0,
  output ld0,
  output ld1,
  output ld2,
  output ld3
);

  wire and_1_out, and_2_out, and_3_out, and_4_out, nor_1_out, not_1_out, not_2_out, not_3_out, not_4_out,
       not_5_out, or_1_out, or_2_out;

  not not_1 (not_1_out, op1);
  not not_2 (not_2_out, op3);
  not not_3 (not_3_out, op2);
  and and_1 (and_1_out, not_2_out, not_3_out, not_4_out, op0);
  not not_4 (not_4_out, op1);
  and and_2 (and_2_out, op3, not_5_out, op1);
  not not_5 (not_5_out, op2);
  and and_3 (and_3_out, op3, op2, not_1_out);
  and and_4 (and_4_out, op3, op2, op1, op0);
  nor nor_1 (nor_1_out, op3, op2, op1, op0);
  or or_1 (or_1_out, and_1_out, and_2_out, and_3_out, and_4_out);
  or or_2 (or_2_out, or_1_out, nor_1_out);
  dec dec_1 (.in_1(or_2_out), .in_2(ora1), .in_3(ora0), .out_4(ld0), .out_5(ld1), .out_6(ld2), .out_7(ld3));
endmodule

module ldo (
  input  op3,
  input  op2,
  input  op1,
  input  op0,
  output ldo
);

  wire and_1_out;

  not not_1 (ldo, and_1_out);
  and and_1 (and_1_out, op3, op2, op1, op0);
endmodule

module ldpc (
  input  op3,
  input  op2,
  input  op1,
  input  op0,
  input  ZF,
  input  OF,
  input  SF,
  output ldpc
);

  wire and_1_out, and_2_out, and_3_out, and_4_out, and_5_out, and_6_out, and_7_out, and_8_out, and_9_out,
       nor_1_out, not_1_out, not_2_out, not_3_out, not_4_out, not_5_out, not_6_out, not_7_out, not_8_out,
       not_9_out, not_10_out, or_1_out;

  not not_1 (not_1_out, op1);
  not not_2 (not_2_out, op0);
  not not_3 (not_3_out, op1);
  not not_4 (not_4_out, op3);
  not not_5 (not_5_out, op2);
  and and_1 (and_1_out, not_4_out, not_5_out, not_6_out, op0);
  not not_6 (not_6_out, op1);
  not not_7 (not_7_out, op2);
  and and_2 (and_2_out, op3, not_7_out, op1, op0);
  not not_8 (not_8_out, op2);
  and and_3 (and_3_out, op3, not_8_out, op1, not_9_out);
  not not_9 (not_9_out, op0);
  and and_4 (and_4_out, op3, op2, not_1_out, not_2_out);
  nor nor_1 (nor_1_out, ZF, SF);
  and and_5 (and_5_out, op3, op2, not_3_out, op0);
  and and_6 (and_6_out, and_2_out, not_10_out);
  not not_10 (not_10_out, OF);
  and and_7 (and_7_out, and_3_out, ZF);
  and and_8 (and_8_out, and_4_out, SF);
  and and_9 (and_9_out, and_5_out, nor_1_out);
  or or_1 (or_1_out, and_1_out, and_6_out, and_7_out, and_8_out);
  nor nor_2 (ldpc, or_1_out, and_9_out);
endmodule

module sela (
  input  op3,
  input  op2,
  input  op1,
  input  op0,
  input  ora1,
  input  ora0,
  input  orb1,
  input  orb0,
  output sela2,
  output sela1,
  output sela0
);

  wire and_1_out, and_2_out, and_3_out, and_4_out, and_5_out, and_6_out, and_7_out, and_8_out, and_9_out,
       and_10_out, and_11_out, and_12_out, and_13_out, and_14_out, and_15_out, and_16_out, and_17_out,
       and_18_out, and_19_out, and_20_out, and_21_out, and_22_out, and_23_out, and_24_out, and_25_out,
       and_26_out, not_1_out, not_2_out, not_3_out, not_4_out, not_5_out, not_6_out, not_7_out, not_8_out,
       not_9_out, not_10_out, not_11_out, not_12_out, not_13_out, not_14_out, not_15_out, not_16_out,
       or_1_out, or_2_out;

  not not_1 (not_1_out, op3);
  not not_2 (not_2_out, op2);
  and and_1 (and_1_out, not_1_out, not_2_out, op0);
  and and_2 (and_2_out, op3, not_3_out, op1);
  not not_3 (not_3_out, op2);
  and and_3 (and_3_out, op3, op2, not_4_out);
  not not_4 (not_4_out, op1);
  not not_5 (not_5_out, op3);
  and and_4 (and_4_out, not_5_out, op2);
  not not_6 (not_6_out, op2);
  and and_5 (and_5_out, op3, not_6_out, not_7_out);
  not not_7 (not_7_out, op1);
  and and_6 (and_6_out, op3, op2, op1);
  and and_7 (and_7_out, op3, op2, op1);
  not not_8 (not_8_out, op0);
  not not_9 (not_9_out, op3);
  and and_8 (and_8_out, not_9_out, not_10_out);
  not not_10 (not_10_out, op2);
  and and_9 (and_9_out, op1, not_11_out);
  not not_11 (not_11_out, op0);
  or or_1 (or_1_out, and_4_out, and_5_out, and_10_out);
  and and_10 (and_10_out, and_6_out, op0);
  and and_11 (and_11_out, and_7_out, not_8_out);
  and and_12 (and_12_out, and_8_out, and_9_out);
  or or_2 (or_2_out, and_1_out, and_2_out, and_3_out);
  not not_12 (not_12_out, or_1_out);
  and and_13 (and_13_out, or_1_out, ora1);
  and and_14 (and_14_out, or_1_out, ora0);
  not not_13 (not_13_out, and_11_out);
  not not_14 (not_14_out, and_11_out);
  and and_15 (and_15_out, or_2_out, or_2_out);
  not not_15 (not_15_out, or_2_out);
  and and_16 (and_16_out, not_15_out, or_2_out);
  and and_17 (and_17_out, or_2_out, or_2_out);
  and and_18 (and_18_out, not_12_out, or_1_out);
  and and_19 (and_19_out, and_13_out, or_1_out);
  and and_20 (and_20_out, and_14_out, or_1_out);
  and and_21 (and_21_out, and_11_out, and_11_out);
  and and_22 (and_22_out, not_13_out, and_11_out);
  and and_23 (and_23_out, not_14_out, and_11_out);
  not not_16 (not_16_out, and_12_out);
  and and_24 (and_24_out, and_12_out, orb1);
  and and_25 (and_25_out, orb0, and_12_out);
  and and_26 (and_26_out, and_12_out, not_16_out);
  or or_3 (sela2, and_26_out, and_21_out, and_18_out, and_15_out);
  or or_4 (sela1, and_24_out, and_22_out, and_19_out, and_16_out);
  or or_5 (sela0, and_25_out, and_23_out, and_20_out, and_17_out);
endmodule

module selb (
  input  op3,
  input  op2,
  input  op1,
  input  op0,
  input  orb1,
  input  orb0,
  output selb2,
  output selb1,
  output selb0
);

  wire and_1_out, and_2_out, and_3_out, and_4_out, and_5_out, and_6_out, and_7_out, and_8_out, and_9_out,
       and_10_out, and_11_out, and_12_out, and_13_out, and_14_out, and_15_out, and_16_out, and_17_out,
       and_18_out, not_1_out, not_2_out, not_3_out, not_4_out, not_5_out, not_6_out, not_7_out, not_8_out,
       not_9_out, not_10_out, not_11_out, not_12_out, not_13_out, not_14_out, or_1_out, or_2_out, or_3_out;

  not not_1 (not_1_out, op2);
  not not_2 (not_2_out, op1);
  not not_3 (not_3_out, op2);
  not not_4 (not_4_out, op1);
  and and_1 (and_1_out, op3, not_5_out, op1);
  not not_5 (not_5_out, op2);
  and and_2 (and_2_out, op3, op2);
  not not_6 (not_6_out, op3);
  and and_3 (and_3_out, not_6_out, not_7_out);
  not not_7 (not_7_out, op2);
  not not_8 (not_8_out, op3);
  and and_4 (and_4_out, not_8_out, op2, op0);
  and and_5 (and_5_out, op3, not_1_out, not_2_out);
  and and_6 (and_6_out, and_5_out, op0);
  not not_9 (not_9_out, op3);
  and and_7 (and_7_out, not_9_out, op2, not_10_out);
  not not_10 (not_10_out, op0);
  and and_8 (and_8_out, op3, not_3_out, not_4_out);
  and and_9 (and_9_out, and_8_out, not_11_out);
  not not_11 (not_11_out, op0);
  or or_1 (or_1_out, and_4_out, and_6_out);
  or or_2 (or_2_out, and_7_out, and_9_out);
  or or_3 (or_3_out, and_1_out, and_2_out, and_3_out);
  and and_10 (and_10_out, or_1_out, or_1_out);
  and and_11 (and_11_out, or_1_out, not_12_out);
  not not_12 (not_12_out, or_1_out);
  and and_12 (and_12_out, or_1_out, or_1_out);
  and and_13 (and_13_out, or_2_out, not_13_out);
  not not_13 (not_13_out, or_2_out);
  and and_14 (and_14_out, or_2_out, orb1);
  and and_15 (and_15_out, or_2_out, orb0);
  and and_16 (and_16_out, or_3_out, or_3_out);
  and and_17 (and_17_out, or_3_out, or_3_out);
  and and_18 (and_18_out, or_3_out, not_14_out);
  not not_14 (not_14_out, or_3_out);
  or or_4 (selb2, and_13_out, and_10_out, and_16_out);
  or or_5 (selb1, and_14_out, and_11_out, and_17_out);
  or or_6 (selb0, and_15_out, and_12_out, and_18_out);
endmodule

module dec (
  input  in_1,
  input  in_2,
  input  in_3,
  output out_4,
  output out_5,
  output out_6,
  output out_7
);

  wire and_1_out, and_2_out, and_3_out, and_4_out, not_1_out, not_2_out, not_3_out, not_4_out, not_5_out,
       not_6_out, not_7_out, not_8_out;

  not not_1 (not_1_out, in_1);
  not not_2 (not_2_out, in_2);
  not not_3 (not_3_out, in_3);
  not not_4 (not_4_out, in_1);
  not not_5 (not_5_out, in_2);
  not not_6 (not_6_out, in_1);
  not not_7 (not_7_out, in_3);
  not not_8 (not_8_out, in_1);
  and and_1 (and_1_out, not_1_out, not_2_out, not_3_out);
  and and_2 (and_2_out, not_4_out, not_5_out, in_3);
  and and_3 (and_3_out, not_6_out, in_2, not_7_out);
  and and_4 (and_4_out, not_8_out, in_2, in_3);
  not not_9 (out_4, and_1_out);
  not not_10 (out_5, and_2_out);
  not not_11 (out_6, and_3_out);
  not not_12 (out_7, and_4_out);
endmodule

module alpm (
  input  op3,
  input  op2,
  input  op1,
  output out_4,
  output A_L
);

  wire not_1_out, not_2_out, not_3_out;

  not not_1 (not_1_out, op3);
  not not_2 (not_2_out, op2);
  not not_3 (not_3_out, op1);
  and and_1 (out_4, not_1_out, op2, op1);
  and and_2 (A_L, op3, not_2_out, not_3_out);
endmodule
